# Fritzing sketch jqflag (saved by Fritzing 0.9.3b)
breadboards: 1

parts:
  Part1 = Arduino Board Ethernet
  J1 = Basic Servo
  U1 = SWITCH_SPDT [package=kps-1290]

nets:
  N1: Part1.D9_PWM, J1.pulse
  N2: Part1.D2_PWM, U1.S
  N3: Part1.D7, U1.O
  5V: Part1.5V, J1.vcc
  GND: Part1.GND, J1.gnd, U1.P
